# Fritzing sketch mega-wiring (saved by Fritzing 0.9.3b)
breadboards: 1

parts:
  Part1 = Arduino Mega 2560 (Rev3)
  R1 = Resistor [tolerance=±5% resistance=68 power=0.25W package=THT]
  LED1 = LED - 3mm [color="White (6500K)" package="3 mm [THT]"]
  LED2 = LED - 3mm [color="White (6500K)" package="3 mm [THT]"]
  R2 = Resistor [tolerance=±5% resistance=68 power=0.25W package=THT]
  R3 = Resistor [tolerance=±5% resistance=68 power=0.25W package=THT]
  R4 = Resistor [tolerance=±5% resistance=68 power=0.25W package=THT]
  R5 = Resistor [tolerance=±5% resistance=68 power=0.25W package=THT]
  LED3 = LED - 3mm [color="White (6500K)" package="3 mm [THT]"]
  LED4 = LED - 3mm [color="White (6500K)" package="3 mm [THT]"]
  LED5 = LED - 3mm [color="White (6500K)" package="3 mm [THT]"]

nets:
  GND: Part1.GND, R1.Pin_0, R2.Pin_0, R3.Pin_0, R4.Pin_0, R5.Pin_0
  N1: Part1.D2_PWM, LED5.anode
  N2: Part1.D3_PWM, LED4.anode
  N3: Part1.D4_PWM, LED3.anode
  N4: Part1.D5_PWM, LED2.anode
  N5: Part1.D6_PWM, LED1.anode
  N6: R1.Pin_1, LED1.cathode
  N7: LED2.cathode, R2.Pin_1
  N8: R3.Pin_1, LED3.cathode
  N9: R4.Pin_1, LED4.cathode
  N10: R5.Pin_1, LED5.cathode
